# Fritzing sketch Head electronics (saved by Fritzing 0.9.6b)
breadboards: 1

parts:
  NEOPIXEL2 = Neopixel Strip -- Black (60/m) [part_number=1461]
  NEOPIXEL3 = Neopixel Strip -- Black (60/m) [part_number=1461]
  Mic1 = KY-038
  R2 = Resistor [tolerance=±5% power=0.25 resistance=220 package=THT]
  Part9 = I2C level shifter bidirectional
  LED3 = LED - 3mm [color="Blue (430nm)" current=0.030 package="3 mm [THT]"]
  LED4 = LED - 3mm [color="Blue (430nm)" current=0.030 package="3 mm [THT]"]

nets:
  +5V: NEOPIXEL2.+5V, NEOPIXEL3.+5V
  N1: NEOPIXEL2.DI, NEOPIXEL3.DI, Part9.HV1
  GND: NEOPIXEL2.GND, NEOPIXEL3.GND
  N2: Mic1.pin2, Part9.GND
  N3: Mic1.pin3, Part9.HV
  N4: Mic1.pin4, Part9.HV2
  N5: R2.Pin_0, LED3.anode, LED4.anode
  N6: R2.Pin_1, Part9.HV3

notes:
  Adafruit bonnet connects Pi to mic and speaker
  [0.5m]
  [0.3m]

custom parts:
  Neopixel Strip -- Black (60/m): Neopixel Strip, Black, 60 pixels per meter.
  KY-038: ky-038 Microphone sound sensor module
